// Logisim project Lab-2-Given.circ as structural Verilog: 8 circuits, main circuit Main
module Main (
);

  wire alu_1_zero, ALUsrc, BEQ, branch, clock_1_out, destSelect, jal, jr, jump, memRead, memToReg, memWrite,
       regWrite;
  wire [3:0] ALUCtrl;
  wire [4:0] _6_10, _11_15, _16_20, _21_25, WrAddr;
  wire [5:0] _0_5, _26_31;
  wire [7:0] PC_out_3;
  wire [31:0] alu_1_aluresult, bit_extender_1_out, ram_1_data, RdData1, RdData2, RdData2ForALU, WrData;

  PC PC (.Offset({_11_15, _6_10, _0_5}), .BEQ(BEQ), .out_3(PC_out_3));
  ALUCtrl aluctrl_1 (
    .OP5(_26_31[5]), .OP4(_26_31[4]), .OP3(_26_31[3]), .OP2(_26_31[2]), .OP1(_26_31[1]), .OP0(_26_31[0]),
    .FUNC5(_0_5[5]), .FUNC4(_0_5[4]), .FUNC3(_0_5[3]), .FUNC2(_0_5[2]), .FUNC1(_0_5[1]), .FUNC0(_0_5[0]),
    .ALUCtrl3(ALUCtrl[3]), .ALUCtrl2(ALUCtrl[2]), .ALUCtrl1(ALUCtrl[1]), .ALUCtrl0(ALUCtrl[0]));  // open: selectDest, writeActivator
  Multiplexer #(.width(5)) multiplexer_1 (.in0(_16_20), .in1(_11_15), .out(WrAddr), .sel(destSelect));  // open: en
  // Probe on WrAddr
  ROM #(.dataWidth(32)) rom_1 (.addr(PC_out_3), .data({_26_31, _21_25, _16_20, _11_15, _6_10, _0_5}));  // open: sel
  Control_Unit control_unit_1 (
    .OP5(_26_31[5]), .OP4(_26_31[4]), .OP3(_26_31[3]), .OP2(_26_31[2]), .OP1(_26_31[1]), .OP0(_26_31[0]),
    .FUNC5(_0_5[5]), .FUNC4(_0_5[4]), .FUNC3(_0_5[3]), .FUNC2(_0_5[2]), .FUNC1(_0_5[1]), .FUNC0(_0_5[0]),
    .selectDest(destSelect), .regWrite(regWrite), .Jump(jump), .JAL(jal), .JR(jr), .Branch(branch),
    .memToReg(memToReg), .memRead(memRead), .memWrite(memWrite), .ALUsrc(ALUsrc));  // open: ALUCtrl3, ALUCtrl2, ALUCtrl1, ALUCtrl0
  assign bit_extender_1_out = {{16{_11_15[4]}}, {_11_15, _6_10, _0_5}};  // Bit_Extender bit_extender_1
  // Probe on RdData1
  // Probe on RdData2ForALU
  Multiplexer #(.width(32)) multiplexer_2 (
    .in0(RdData2), .in1(bit_extender_1_out), .out(RdData2ForALU), .sel(ALUsrc));  // open: en
  // Probe on RdData2ForALU
  ALU alu_1 (
    .ALUCtl(ALUCtrl), .A(RdData1), .B(RdData2ForALU), .ALUResult(alu_1_aluresult), .Zero(alu_1_zero),
    .Shamt({5{1'b0}}));  // open: Overflow
  // Probe on nothing
  // Probe on nothing
  // Probe on nothing
  // Probe on nothing
  // Probe on nothing
  // Probe on nothing
  // Probe on nothing
  // Probe on nothing
  // Probe on nothing
  // Probe on nothing
  and and_1 (BEQ, branch, alu_1_zero);
  // Probe on alu_1_aluresult
  Register_File register_file_1 (
    .WrAddr(WrAddr), .WrData(WrData), .WrReg(regWrite), .RdAddr1(_21_25), .RdAddr2(_16_20),
    .RdData1(RdData1), .RdData2(RdData2), .Clock(clock_1_out));
  Clock clock_1 (.out(clock_1_out));
  // Probe on RdData1
  // Probe on RdData2
  RAM #(.dataWidth(32), .bus("separate")) ram_1 (
    .addr(alu_1_aluresult[7:0]), .din(RdData2), .data(ram_1_data), .str(memWrite), .ld(memRead));  // open: sel, clk, clr
  // Probe on ram_1_data
  Multiplexer #(.width(32)) multiplexer_3 (
    .in0(alu_1_aluresult), .in1(ram_1_data), .out(WrData), .sel(memToReg));  // open: en

  // Notes on the sheet:
  //   opcode
  //   r_func
  //   rtype if destSelect is 1
  //   immediate operand / offset for BEQ
  //   opcode
  //   r_func
  //   Which register address R type or I type
  //   contents of rom_1 (hex, n*v repeats v):
  //   20010008 34220005 3043ffff 612020 832822 223024 c33826 aca40064 8ca80064 22482a 1265025 214bfff6
  //   10b602b c00000f 200d0001 23ff0018 10c00003 a13022 8000010 200e0001 3e00008 200f0001 20100001
  //   If ALUsrc is 1 means value is immediate
  //   sourceReg 21-25
  //   5-bit address to write to
  //   32-bit data to write
  //   read into address
  //   what to read in
endmodule

module _32_Bit_Adder_Subtractor (
  input  Add_Sub_control,
  input  [31:0] in_2,
  input  [31:0] in_3,
  output [31:0] out_4,
  output carry_out
);

  wire adder_1_cout, subtractor_1_bout;
  wire [31:0] adder_1_out, subtractor_1_out;

  Adder #(.width(32)) adder_1 (.a(in_2), .b(in_3), .out(adder_1_out), .cout(adder_1_cout));  // open: cin
  Subtractor #(.width(32)) subtractor_1 (
    .a(in_2), .b(in_3), .out(subtractor_1_out), .bout(subtractor_1_bout));  // open: bin
  Multiplexer #(.width(32), .enable("false")) multiplexer_1 (
    .in0(adder_1_out), .in1(subtractor_1_out), .out(out_4), .sel(Add_Sub_control));
  Multiplexer #(.enable("false")) multiplexer_2 (
    .in0(adder_1_cout), .in1(subtractor_1_bout), .out(carry_out), .sel(Add_Sub_control));
endmodule

module ALU (
  input  [3:0] ALUCtl,
  input  [31:0] A,
  input  [31:0] B,
  input  [4:0] Shamt,
  output [31:0] ALUResult,
  output Zero,
  output Overflow
);

  wire comparator_1_lt, comparator_2_lt, comparator_3_eq, comparator_4_eq, or_2_out;
  wire [31:0] Add, And, LessThan, LessThanUnsigned, Nor, Or, ShiftLeft, ShiftRight, Sub, Xor;

  // Probe on ALUCtl
  assign Nor = ~(A | B);  // NOR_Gate nor_1, 32 bits wide
  Adder #(.width(32)) adder_1 (.a(A), .b(B), .out(Add));  // open: cin, cout
  Subtractor #(.width(32)) subtractor_1 (.a(A), .b(B), .out(Sub));  // open: bin, bout
  assign And = A & B;  // AND_Gate and_1, 32 bits wide
  assign Or = A | B;  // OR_Gate or_1, 32 bits wide
  assign Xor = A ^ B;  // XOR_Gate xor_1, 32 bits wide
  Comparator #(.width(32)) comparator_1 (.a(A), .b(B), .lt(comparator_1_lt));  // open: gt, eq
  assign LessThan = {{31{1'b0}}, comparator_1_lt};  // Bit_Extender bit_extender_1
  Shifter #(.width(32)) shifter_1 (.in(B), .\dist (Shamt), .out(ShiftLeft));
  Shifter #(.width(32), .shift("lr")) shifter_2 (.in(B), .\dist (Shamt), .out(ShiftRight));
  Comparator #(.width(32), .mode("unsigned")) comparator_2 (.a(A), .b(B), .lt(comparator_2_lt));  // open: gt, eq
  assign LessThanUnsigned = {{31{1'b0}}, comparator_2_lt};  // Bit_Extender bit_extender_2
  Multiplexer #(.select(4), .width(32), .enable("false")) multiplexer_1 (
    .in0(Or), .in1(LessThanUnsigned), .in2(LessThan), .in3(Add), .in4(Sub), .in5(Xor), .in6(And),
    .in14(ShiftRight), .in15(ShiftLeft), .out(ALUResult), .sel(ALUCtl));  // open: in7, in8, in9, in10, in11, in12, in13
  Comparator #(.width(4)) comparator_3 (.a(4'b0011), .b(ALUCtl), .eq(comparator_3_eq));  // open: gt, lt
  Comparator #(.width(4)) comparator_4 (.a(ALUCtl), .b(4'b0100), .eq(comparator_4_eq));  // open: gt, lt
  Overflow_Unit overflow_unit_1 (
    .Add(comparator_3_eq), .Sub(comparator_4_eq), .ASign(A[31]), .BSign(B[31]), .ResultSign(ALUResult[31]),
    .Overflow(Overflow));
  or or_2 (or_2_out, ALUResult[0], ALUResult[1], ALUResult[2], ALUResult[3], ALUResult[4], ALUResult[5], ALUResult[6], ALUResult[7], ALUResult[8], ALUResult[9], ALUResult[10], ALUResult[11], ALUResult[12], ALUResult[13], ALUResult[14], ALUResult[15], ALUResult[16], ALUResult[17], ALUResult[18], ALUResult[19], ALUResult[20], ALUResult[21], ALUResult[22], ALUResult[23], ALUResult[24], ALUResult[25], ALUResult[26], ALUResult[27], ALUResult[28], ALUResult[29], ALUResult[30], ALUResult[31]);
  not not_1 (Zero, or_2_out);

  // Other names for the same wires on the sheet: ASign = A[31]; ResultSign = ALUResult[31]; BSign = B[31]

  // Notes on the sheet:
  //   ALUCtl for ADD for top port
  //   ALUCtl for SUB for second port
endmodule

module Register_File (
  input  [4:0] WrAddr,
  input  [31:0] WrData,
  input  WrReg,
  input  [4:0] RdAddr1,
  input  [4:0] RdAddr2,
  input  Clock,
  output [31:0] RdData1,
  output [31:0] RdData2
);

  wire WrReg0, WrReg1, WrReg2, WrReg3, WrReg4, WrReg5, WrReg6, WrReg7, WrReg8, WrReg9, WrReg10, WrReg11,
       WrReg12, WrReg13, WrReg14, WrReg15, WrReg16, WrReg17, WrReg18, WrReg19, WrReg20, WrReg21, WrReg22,
       WrReg23, WrReg24, WrReg25, WrReg26, WrReg27, WrReg28, WrReg29, WrReg30, WrReg31;
  wire [31:0] RegData1, RegData2, RegData3, RegData4, RegData5, RegData6, RegData7, RegData8, RegData9,
       RegData10, RegData11, RegData12, RegData13, RegData14, RegData15, RegData16, RegData17, RegData18,
       RegData19, RegData20, RegData21, RegData22, RegData23, RegData24, RegData25, RegData26, RegData27,
       RegData28, RegData29, RegData30, RegData31;

  Demultiplexer #(.select(5), .enable("false")) demultiplexer_1 (
    .out0(WrReg0), .out1(WrReg1), .out2(WrReg2), .out3(WrReg3), .out4(WrReg4), .out5(WrReg5), .out6(WrReg6),
    .out7(WrReg7), .out8(WrReg8), .out9(WrReg9), .out10(WrReg10), .out11(WrReg11), .out12(WrReg12),
    .out13(WrReg13), .out14(WrReg14), .out15(WrReg15), .out16(WrReg16), .out17(WrReg17), .out18(WrReg18),
    .out19(WrReg19), .out20(WrReg20), .out21(WrReg21), .out22(WrReg22), .out23(WrReg23), .out24(WrReg24),
    .out25(WrReg25), .out26(WrReg26), .out27(WrReg27), .out28(WrReg28), .out29(WrReg29), .out30(WrReg30),
    .out31(WrReg31), .in(WrReg), .sel(WrAddr));
  // Probe on RegData4
  Register #(.width(32)) Reg4 (.D(WrData), .en(WrReg4), .Q(RegData4), .clk(Clock));  // open: clr
  // Probe on RegData8
  Register #(.width(32)) Reg8 (.D(WrData), .en(WrReg8), .Q(RegData8), .clk(Clock));  // open: clr
  // Probe on RegData12
  Register #(.width(32)) Reg12 (.D(WrData), .en(WrReg12), .Q(RegData12), .clk(Clock));  // open: clr
  // Probe on RegData16
  Register #(.width(32)) Reg16 (.D(WrData), .en(WrReg16), .Q(RegData16), .clk(Clock));  // open: clr
  // Probe on RegData20
  Register #(.width(32)) Reg20 (.D(WrData), .en(WrReg20), .Q(RegData20), .clk(Clock));  // open: clr
  // Probe on RegData24
  Register #(.width(32)) Reg24 (.D(WrData), .en(WrReg24), .Q(RegData24), .clk(Clock));  // open: clr
  // Probe on RegData28
  Register #(.width(32)) Reg28 (.D(WrData), .en(WrReg28), .Q(RegData28), .clk(Clock));  // open: clr
  Register #(.width(32)) Reg1 (.D(WrData), .en(WrReg1), .Q(RegData1), .clk(Clock));  // open: clr
  Register #(.width(32)) Reg5 (.D(WrData), .en(WrReg5), .Q(RegData5), .clk(Clock));  // open: clr
  Register #(.width(32)) Reg9 (.D(WrData), .en(WrReg9), .Q(RegData9), .clk(Clock));  // open: clr
  Register #(.width(32)) Reg13 (.D(WrData), .en(WrReg13), .Q(RegData13), .clk(Clock));  // open: clr
  Register #(.width(32)) Reg17 (.D(WrData), .en(WrReg17), .Q(RegData17), .clk(Clock));  // open: clr
  Register #(.width(32)) Reg21 (.D(WrData), .en(WrReg21), .Q(RegData21), .clk(Clock));  // open: clr
  Register #(.width(32)) Reg25 (.D(WrData), .en(WrReg25), .Q(RegData25), .clk(Clock));  // open: clr
  Register #(.width(32)) Reg29 (.D(WrData), .en(WrReg29), .Q(RegData29), .clk(Clock));  // open: clr
  // Probe on RegData1
  // Probe on RegData5
  // Probe on RegData9
  // Probe on RegData13
  // Probe on RegData17
  // Probe on RegData21
  // Probe on RegData25
  // Probe on RegData29
  // Probe on RegData2
  Register #(.width(32)) Reg2 (.D(WrData), .en(WrReg2), .Q(RegData2), .clk(Clock));  // open: clr
  // Probe on RegData6
  Register #(.width(32)) Reg6 (.D(WrData), .en(WrReg6), .Q(RegData6), .clk(Clock));  // open: clr
  // Probe on RegData10
  Register #(.width(32)) Reg10 (.D(WrData), .en(WrReg10), .Q(RegData10), .clk(Clock));  // open: clr
  // Probe on RegData14
  Register #(.width(32)) Reg14 (.D(WrData), .en(WrReg14), .Q(RegData14), .clk(Clock));  // open: clr
  // Probe on RegData18
  Register #(.width(32)) Reg18 (.D(WrData), .en(WrReg18), .Q(RegData18), .clk(Clock));  // open: clr
  // Probe on RegData22
  Register #(.width(32)) Reg22 (.D(WrData), .en(WrReg22), .Q(RegData22), .clk(Clock));  // open: clr
  // Probe on RegData26
  Register #(.width(32)) Reg26 (.D(WrData), .en(WrReg26), .Q(RegData26), .clk(Clock));  // open: clr
  // Probe on RegData30
  Register #(.width(32)) Reg30 (.D(WrData), .en(WrReg30), .Q(RegData30), .clk(Clock));  // open: clr
  // Probe on RegData3
  Register #(.width(32)) Reg3 (.D(WrData), .en(WrReg3), .Q(RegData3), .clk(Clock));  // open: clr
  // Probe on RegData7
  Register #(.width(32)) Reg7 (.D(WrData), .en(WrReg7), .Q(RegData7), .clk(Clock));  // open: clr
  // Probe on RegData11
  Register #(.width(32)) Reg11 (.D(WrData), .en(WrReg11), .Q(RegData11), .clk(Clock));  // open: clr
  // Probe on RegData15
  Register #(.width(32)) Reg15 (.D(WrData), .en(WrReg15), .Q(RegData15), .clk(Clock));  // open: clr
  // Probe on RegData19
  Register #(.width(32)) Reg19 (.D(WrData), .en(WrReg19), .Q(RegData19), .clk(Clock));  // open: clr
  // Probe on RegData23
  Register #(.width(32)) Reg23 (.D(WrData), .en(WrReg23), .Q(RegData23), .clk(Clock));  // open: clr
  // Probe on RegData27
  Register #(.width(32)) Reg27 (.D(WrData), .en(WrReg27), .Q(RegData27), .clk(Clock));  // open: clr
  // Probe on RegData31
  Register #(.width(32)) Reg31 (.D(WrData), .en(WrReg31), .Q(RegData31), .clk(Clock));  // open: clr
  Multiplexer #(.select(5), .width(32), .enable("false")) multiplexer_1 (
    .in0({32{1'b0}}), .in1(RegData1), .in2(RegData2), .in3(RegData3), .in4(RegData4), .in5(RegData5),
    .in6(RegData6), .in7(RegData7), .in8(RegData8), .in9(RegData9), .in10(RegData10), .in11(RegData11),
    .in12(RegData12), .in13(RegData13), .in14(RegData14), .in15(RegData15), .in16(RegData16),
    .in17(RegData17), .in18(RegData18), .in19(RegData19), .in20(RegData20), .in21(RegData21),
    .in22(RegData22), .in23(RegData23), .in24(RegData24), .in25(RegData25), .in26(RegData26),
    .in27(RegData27), .in28(RegData28), .in29(RegData29), .in30(RegData30), .in31(RegData31), .out(RdData1),
    .sel(RdAddr1));
  Multiplexer #(.select(5), .width(32), .enable("false")) multiplexer_2 (
    .in0({32{1'b0}}), .in1(RegData1), .in2(RegData2), .in3(RegData3), .in4(RegData4), .in5(RegData5),
    .in6(RegData6), .in7(RegData7), .in8(RegData8), .in9(RegData9), .in10(RegData10), .in11(RegData11),
    .in12(RegData12), .in13(RegData13), .in14(RegData14), .in15(RegData15), .in16(RegData16),
    .in17(RegData17), .in18(RegData18), .in19(RegData19), .in20(RegData20), .in21(RegData21),
    .in22(RegData22), .in23(RegData23), .in24(RegData24), .in25(RegData25), .in26(RegData26),
    .in27(RegData27), .in28(RegData28), .in29(RegData29), .in30(RegData30), .in31(RegData31), .out(RdData2),
    .sel(RdAddr2));
endmodule

module Overflow_Unit (
  input  Add,
  input  Sub,
  input  ASign,
  input  BSign,
  input  ResultSign,
  output Overflow
);

  wire and_1_out, and_2_out, or_1_out, xnor_1_out, xor_1_out, xor_2_out;

  xnor xnor_1 (xnor_1_out, ASign, BSign);
  xor xor_1 (xor_1_out, ASign, BSign);
  and and_1 (and_1_out, xnor_1_out, Add);
  and and_2 (and_2_out, xor_1_out, Sub);
  or or_1 (or_1_out, and_1_out, and_2_out);
  xor xor_2 (xor_2_out, ResultSign, ASign);
  and and_3 (Overflow, or_1_out, xor_2_out);

  // Notes on the sheet:
  //   Overflow occurs when doing addition and sign(A) == sign(B) && sign(result) != sign(A)
  //   Or
  //   Overflow occurs when doing subtraction and sign(A) != sign(B) && sign(result) != sign(A)
endmodule

module PC (
  input  BEQ,
  input  [15:0] Offset,
  output [7:0] out_3
);

  wire clock_1_out;
  wire [31:0] adder_1_out, bit_extender_1_out, multiplexer_1_out, register_1_q;

  Adder #(.width(32)) adder_1 (
    .a({multiplexer_1_out[31:10], out_3, multiplexer_1_out[1:0]}), .b(32'h4), .out(adder_1_out));  // open: cin, cout
  Register #(.width(32)) register_1 (.D(adder_1_out), .Q(register_1_q), .clk(clock_1_out));  // open: en, clr
  Clock clock_1 (.out(clock_1_out));
  assign bit_extender_1_out = {{16{1'b0}}, Offset};  // Bit_Extender bit_extender_1
  Multiplexer #(.width(32)) multiplexer_1 (
    .in0(register_1_q), .in1(bit_extender_1_out),
    .out({multiplexer_1_out[31:10], out_3, multiplexer_1_out[1:0]}), .sel(BEQ));  // open: en
endmodule

module Control_Unit (
  input  OP5,
  input  OP4,
  input  OP3,
  input  OP2,
  input  OP1,
  input  OP0,
  input  FUNC5,
  input  FUNC4,
  input  FUNC3,
  input  FUNC2,
  input  FUNC1,
  input  FUNC0,
  output ALUCtrl3,
  output ALUCtrl2,
  output ALUCtrl1,
  output ALUCtrl0,
  output selectDest,
  output regWrite,
  output Jump,
  output JAL,
  output JR,
  output Branch,
  output memToReg,
  output memRead,
  output memWrite,
  output ALUsrc
);

  wire and_1_out, and_2_out, and_3_out, and_4_out, and_5_out, and_6_out, and_8_out, and_14_out, and_15_out,
       and_16_out, and_17_out, and_18_out, and_19_out, and_20_out, and_21_out, not_1_out, not_2_out,
       not_3_out, not_4_out, not_5_out, not_6_out, not_7_out, not_8_out, not_9_out, not_10_out, not_11_out,
       not_12_out, not_13_out, not_14_out, not_15_out, not_16_out, not_17_out, not_18_out, not_19_out,
       not_20_out, not_21_out, not_22_out, not_23_out, not_24_out, not_25_out, not_26_out, not_27_out,
       not_28_out, not_29_out, not_30_out, not_31_out, not_32_out, not_33_out, not_34_out, not_35_out,
       not_36_out, not_37_out, not_38_out, not_39_out, not_40_out, not_41_out, not_42_out, not_43_out,
       not_44_out, not_45_out, not_46_out, not_47_out, not_48_out, not_49_out, not_50_out, not_51_out,
       not_52_out, not_53_out, not_54_out, not_55_out, not_56_out, not_57_out, not_58_out, not_59_out,
       not_60_out, not_61_out, not_62_out, not_63_out, not_64_out, not_65_out, not_66_out;

  not not_1 (not_1_out, OP3);
  and and_1 (and_1_out, not_1_out, not_2_out, FUNC1);
  not not_2 (not_2_out, FUNC3);
  not not_3 (not_3_out, OP3);
  and and_2 (and_2_out, not_3_out, FUNC2, not_4_out);
  not not_4 (not_4_out, FUNC0);
  and and_3 (and_3_out, OP2, not_5_out);
  not not_5 (not_5_out, OP0);
  not not_6 (not_6_out, OP3);
  and and_4 (and_4_out, not_6_out, not_7_out, not_8_out);
  not not_7 (not_7_out, FUNC1);
  not not_8 (not_8_out, FUNC0);
  not not_9 (not_9_out, OP3);
  and and_5 (and_5_out, not_9_out, FUNC3, not_10_out);
  not not_10 (not_10_out, FUNC0);
  and and_6 (and_6_out, OP3, not_11_out);
  not not_11 (not_11_out, OP0);
  not not_12 (not_12_out, OP3);
  not not_13 (not_13_out, FUNC2);
  not not_14 (not_14_out, FUNC1);
  not not_15 (not_15_out, OP2);
  not not_16 (not_16_out, FUNC5);
  not not_17 (not_17_out, OP3);
  not not_18 (not_18_out, FUNC2);
  not not_19 (not_19_out, OP3);
  not not_20 (not_20_out, OP5);
  not not_21 (not_21_out, OP4);
  not not_22 (not_22_out, OP2);
  not not_23 (not_23_out, OP1);
  not not_24 (not_24_out, OP0);
  not not_25 (not_25_out, OP3);
  and and_7 (selectDest, not_25_out, not_26_out);
  not not_26 (not_26_out, OP2);
  not not_27 (not_27_out, OP1);
  or or_1 (regWrite, not_27_out, OP3);
  not not_28 (not_28_out, OP5);
  not not_29 (not_29_out, OP4);
  not not_30 (not_30_out, OP3);
  and and_8 (and_8_out, not_28_out, not_29_out, not_30_out, not_31_out, OP1, not_32_out);
  not not_31 (not_31_out, OP2);
  not not_32 (not_32_out, OP0);
  not not_33 (not_33_out, OP5);
  not not_34 (not_34_out, OP4);
  not not_35 (not_35_out, OP3);
  and and_9 (JAL, not_33_out, not_34_out, not_35_out, not_36_out, OP1, OP0);
  not not_36 (not_36_out, OP2);
  not not_37 (not_37_out, OP5);
  not not_38 (not_38_out, OP4);
  not not_39 (not_39_out, OP3);
  not not_40 (not_40_out, OP2);
  not not_41 (not_41_out, OP1);
  not not_42 (not_42_out, OP0);
  and and_10 (JR, not_37_out, not_38_out, not_39_out, not_40_out, not_41_out, not_42_out, not_43_out, not_44_out, FUNC3, not_45_out, not_46_out, not_47_out);
  not not_43 (not_43_out, FUNC5);
  not not_44 (not_44_out, FUNC4);
  not not_45 (not_45_out, FUNC2);
  not not_46 (not_46_out, FUNC1);
  not not_47 (not_47_out, FUNC0);
  not not_48 (not_48_out, OP5);
  not not_49 (not_49_out, OP4);
  not not_50 (not_50_out, OP3);
  and and_11 (Branch, not_48_out, not_49_out, not_50_out, OP2, not_51_out, not_52_out);
  not not_51 (not_51_out, OP1);
  not not_52 (not_52_out, OP0);
  not not_53 (not_53_out, OP4);
  not not_54 (not_54_out, OP3);
  and and_12 (memRead, OP5, not_53_out, not_54_out, not_55_out, OP1, OP0);
  not not_55 (not_55_out, OP2);
  not not_56 (not_56_out, OP4);
  and and_13 (memWrite, OP5, not_56_out, OP3, not_57_out, OP1, OP0);
  not not_57 (not_57_out, OP2);
  not not_58 (not_58_out, OP5);
  not not_59 (not_59_out, OP4);
  and and_14 (and_14_out, not_58_out, not_59_out, OP3, not_60_out, not_61_out);
  not not_60 (not_60_out, OP1);
  not not_61 (not_61_out, OP0);
  not not_62 (not_62_out, OP5);
  not not_63 (not_63_out, OP4);
  and and_15 (and_15_out, not_62_out, not_63_out, OP3, OP2, not_64_out);
  not not_64 (not_64_out, OP1);
  not not_65 (not_65_out, OP4);
  and and_16 (and_16_out, OP5, not_65_out, not_66_out, OP1, OP0);
  not not_66 (not_66_out, OP2);
  or or_2 (ALUCtrl2, and_1_out, and_2_out, and_3_out);
  or or_3 (ALUCtrl1, and_4_out, and_5_out, and_6_out);
  and and_17 (and_17_out, not_12_out, not_13_out, not_14_out);
  and and_18 (and_18_out, not_15_out, not_16_out);
  and and_19 (and_19_out, not_17_out, not_18_out, FUNC0);
  and and_20 (and_20_out, not_19_out, FUNC2, FUNC1);
  and and_21 (and_21_out, not_20_out, not_21_out, OP3, not_22_out, not_23_out, not_24_out);
  or or_4 (ALUsrc, and_14_out, and_15_out, and_16_out);
  or or_5 (ALUCtrl0, and_17_out, and_18_out, and_19_out, and_20_out, and_21_out);
  or or_6 (Jump, and_8_out, JAL);

  assign ALUCtrl3 = 1'b0;
  assign memToReg = memRead;
endmodule

module ALUCtrl (
  input  OP5,
  input  OP4,
  input  OP3,
  input  OP2,
  input  OP1,
  input  OP0,
  input  FUNC5,
  input  FUNC4,
  input  FUNC3,
  input  FUNC2,
  input  FUNC1,
  input  FUNC0,
  output ALUCtrl3,
  output ALUCtrl2,
  output ALUCtrl1,
  output ALUCtrl0,
  output selectDest,
  output writeActivator
);

  wire and_1_out, and_2_out, and_3_out, and_5_out, and_6_out, and_7_out, and_8_out, and_9_out, and_10_out,
       and_11_out, and_12_out, and_13_out, and_14_out, and_15_out, and_16_out, and_17_out, and_18_out,
       and_19_out, and_20_out, and_21_out, and_22_out, and_23_out, and_24_out, and_25_out, and_26_out,
       and_27_out, and_28_out, and_29_out, and_30_out, and_31_out, and_32_out, not_1_out, not_2_out,
       not_3_out, not_4_out, not_5_out, not_6_out, not_7_out, not_8_out, not_9_out, not_10_out, not_11_out,
       not_12_out, not_13_out, not_14_out, not_15_out, not_16_out, not_17_out, not_18_out, not_19_out,
       not_20_out, not_21_out, not_22_out, not_23_out, not_24_out, not_25_out, not_26_out, not_27_out,
       not_28_out, not_29_out, not_30_out, not_31_out, not_32_out, not_33_out, not_34_out, not_35_out,
       not_36_out, not_37_out, not_38_out, not_39_out, not_40_out, not_41_out, not_42_out, not_43_out,
       not_44_out, not_45_out, not_46_out, not_47_out, not_48_out, not_49_out, not_50_out, not_51_out,
       not_52_out, not_53_out, not_54_out, not_55_out, not_56_out, not_57_out, not_58_out, not_59_out,
       not_60_out, not_61_out, not_62_out, not_63_out, not_64_out, not_65_out, not_66_out, not_67_out,
       not_68_out, not_69_out, not_70_out, not_71_out, not_72_out, not_73_out, not_74_out, not_75_out,
       not_76_out;

  not not_1 (not_1_out, OP3);
  not not_2 (not_2_out, FUNC3);
  and and_1 (and_1_out, not_1_out, not_2_out, FUNC1);
  not not_3 (not_3_out, OP3);
  and and_2 (and_2_out, not_3_out, FUNC2, not_4_out);
  not not_4 (not_4_out, FUNC0);
  and and_3 (and_3_out, OP2, not_5_out);
  not not_5 (not_5_out, OP0);
  not not_6 (not_6_out, OP2);
  not not_7 (not_7_out, OP0);
  not not_8 (not_8_out, FUNC1);
  not not_9 (not_9_out, FUNC0);
  not not_10 (not_10_out, OP3);
  not not_11 (not_11_out, OP2);
  not not_12 (not_12_out, FUNC0);
  not not_13 (not_13_out, OP3);
  not not_14 (not_14_out, FUNC1);
  not not_15 (not_15_out, FUNC0);
  not not_16 (not_16_out, OP3);
  not not_17 (not_17_out, FUNC0);
  not not_18 (not_18_out, OP0);
  not not_19 (not_19_out, FUNC1);
  not not_20 (not_20_out, FUNC0);
  not not_21 (not_21_out, OP0);
  not not_22 (not_22_out, FUNC0);
  not not_23 (not_23_out, OP0);
  not not_24 (not_24_out, OP0);
  not not_25 (not_25_out, FUNC1);
  not not_26 (not_26_out, FUNC0);
  not not_27 (not_27_out, OP0);
  not not_28 (not_28_out, FUNC0);
  not not_29 (not_29_out, OP0);
  not not_30 (not_30_out, FUNC1);
  not not_31 (not_31_out, FUNC0);
  not not_32 (not_32_out, OP0);
  not not_33 (not_33_out, FUNC0);
  not not_34 (not_34_out, OP3);
  not not_35 (not_35_out, OP2);
  not not_36 (not_36_out, FUNC2);
  not not_37 (not_37_out, FUNC1);
  not not_38 (not_38_out, OP2);
  not not_39 (not_39_out, FUNC5);
  not not_40 (not_40_out, OP3);
  not not_41 (not_41_out, OP2);
  not not_42 (not_42_out, FUNC2);
  not not_43 (not_43_out, OP3);
  not not_44 (not_44_out, OP2);
  not not_45 (not_45_out, OP3);
  not not_46 (not_46_out, FUNC2);
  not not_47 (not_47_out, FUNC1);
  not not_48 (not_48_out, OP3);
  not not_49 (not_49_out, FUNC2);
  not not_50 (not_50_out, OP3);
  not not_51 (not_51_out, OP3);
  not not_52 (not_52_out, FUNC2);
  not not_53 (not_53_out, FUNC1);
  not not_54 (not_54_out, OP3);
  not not_55 (not_55_out, FUNC2);
  not not_56 (not_56_out, OP3);
  not not_57 (not_57_out, OP5);
  not not_58 (not_58_out, OP4);
  not not_59 (not_59_out, OP2);
  not not_60 (not_60_out, OP1);
  not not_61 (not_61_out, OP0);
  not not_62 (not_62_out, OP3);
  not not_63 (not_63_out, FUNC2);
  not not_64 (not_64_out, FUNC1);
  not not_65 (not_65_out, OP3);
  not not_66 (not_66_out, FUNC2);
  not not_67 (not_67_out, OP3);
  not not_68 (not_68_out, OP3);
  not not_69 (not_69_out, FUNC2);
  not not_70 (not_70_out, FUNC1);
  not not_71 (not_71_out, OP3);
  not not_72 (not_72_out, FUNC2);
  not not_73 (not_73_out, OP3);
  not not_74 (not_74_out, OP3);
  and and_4 (selectDest, not_74_out, not_75_out);
  not not_75 (not_75_out, OP2);
  not not_76 (not_76_out, OP1);
  or or_1 (writeActivator, not_76_out, OP3);
  or or_2 (ALUCtrl2, and_1_out, and_2_out, and_3_out);
  and and_5 (and_5_out, not_6_out, not_7_out, not_8_out, not_9_out);
  and and_6 (and_6_out, not_10_out, not_11_out, FUNC3, not_12_out);
  and and_7 (and_7_out, not_13_out, OP0, not_14_out, not_15_out);
  and and_8 (and_8_out, not_16_out, OP0, FUNC3, not_17_out);
  and and_9 (and_9_out, OP1, not_18_out, not_19_out, not_20_out);
  and and_10 (and_10_out, OP1, not_21_out, FUNC3, not_22_out);
  and and_11 (and_11_out, OP3, not_23_out);
  and and_12 (and_12_out, OP4, not_24_out, not_25_out, not_26_out);
  and and_13 (and_13_out, OP4, not_27_out, FUNC3, not_28_out);
  and and_14 (and_14_out, OP5, not_29_out, not_30_out, not_31_out);
  and and_15 (and_15_out, OP5, not_32_out, FUNC3, not_33_out);
  and and_16 (and_16_out, not_34_out, not_35_out, not_36_out, not_37_out);
  and and_17 (and_17_out, not_38_out, not_39_out);
  and and_18 (and_18_out, not_40_out, not_41_out, not_42_out, FUNC0);
  and and_19 (and_19_out, not_43_out, not_44_out, FUNC2, FUNC1);
  and and_20 (and_20_out, not_45_out, OP0, not_46_out, not_47_out);
  and and_21 (and_21_out, not_48_out, OP0, not_49_out, FUNC0);
  and and_22 (and_22_out, not_50_out, OP0, FUNC2, FUNC1);
  and and_23 (and_23_out, not_51_out, OP1, not_52_out, not_53_out);
  and and_24 (and_24_out, not_54_out, OP1, not_55_out, FUNC0);
  and and_25 (and_25_out, not_56_out, OP1, FUNC2, FUNC1);
  and and_26 (and_26_out, not_57_out, not_58_out, OP3, not_59_out, not_60_out, not_61_out);
  and and_27 (and_27_out, OP4, not_62_out, not_63_out, not_64_out);
  and and_28 (and_28_out, OP4, not_65_out, not_66_out, FUNC0);
  and and_29 (and_29_out, OP4, not_67_out, FUNC2, FUNC1);
  and and_30 (and_30_out, OP5, not_68_out, not_69_out, not_70_out);
  and and_31 (and_31_out, OP5, not_71_out, not_72_out, FUNC0);
  and and_32 (and_32_out, OP5, not_73_out, FUNC2, FUNC1);
  or or_3 (ALUCtrl1, and_5_out, and_6_out, and_7_out, and_8_out, and_9_out, and_10_out, and_11_out, and_12_out, and_13_out, and_14_out, and_15_out);
  or or_4 (ALUCtrl0, and_16_out, and_17_out, and_18_out, and_19_out, and_20_out, and_21_out, and_22_out, and_23_out, and_24_out, and_25_out, and_26_out, and_27_out, and_28_out, and_29_out, and_30_out, and_31_out, and_32_out);

  assign ALUCtrl3 = 1'b0;
endmodule
